// Logisim project Karnaugh R1.circ as structural Verilog: 1 circuit, main circuit main
module main (
  input  A1,
  input  A2,
  input  B1,
  input  B2,
  output R1
);

  wire and_1_out, and_2_out;

  and and_1 (and_1_out, A1, A2);
  and and_2 (and_2_out, B1, B2);
  and and_3 (R1, and_1_out, and_2_out);

  // Notes on the sheet:
  //   Karnaugh R1
endmodule
