// Logisim project Karnaugh R2.circ as structural Verilog: 1 circuit, main circuit main
module main (
  input  A1,
  input  A2,
  input  B1,
  input  B2,
  output R2
);

  wire and_1_out, and_2_out, and_3_out, and_4_out, not_1_out, not_2_out;

  not not_1 (not_1_out, A2);
  not not_2 (not_2_out, B2);
  and and_1 (and_1_out, A1, not_1_out);
  and and_2 (and_2_out, A1, B1);
  and and_3 (and_3_out, and_1_out, B1);
  and and_4 (and_4_out, and_2_out, not_2_out);
  or or_1 (R2, and_3_out, and_4_out);

  // Notes on the sheet:
  //   Karnaugh R2
endmodule
