// Logisim project Questão 05.circ as structural Verilog: 1 circuit, main circuit main
module main (
  input  A1,
  input  A2,
  input  B1,
  input  B2,
  output R1,
  output R2,
  output R3,
  output R4
);

  wire and_1_out, and_2_out, and_4_out, and_5_out, and_6_out, and_7_out, and_8_out, and_9_out, and_10_out,
       and_11_out, and_12_out, and_13_out, and_14_out, and_15_out, not_1_out, not_2_out, not_3_out,
       not_4_out, not_5_out, not_6_out, or_1_out, or_3_out;

  and and_1 (and_1_out, A1, A2);
  and and_2 (and_2_out, B1, B2);
  not not_1 (not_1_out, B2);
  not not_2 (not_2_out, A1);
  and and_3 (R1, and_1_out, and_2_out);
  not not_3 (not_3_out, A2);
  not not_4 (not_4_out, B2);
  not not_5 (not_5_out, B1);
  not not_6 (not_6_out, A2);
  and and_4 (and_4_out, A2, B1);
  and and_5 (and_5_out, not_2_out, A2);
  and and_6 (and_6_out, A1, not_3_out);
  and and_7 (and_7_out, A1, B1);
  and and_8 (and_8_out, A1, not_5_out);
  and and_9 (and_9_out, A1, not_6_out);
  and and_10 (and_10_out, and_4_out, not_1_out);
  and and_11 (and_11_out, and_5_out, B1);
  and and_12 (and_12_out, and_6_out, B1);
  and and_13 (and_13_out, and_7_out, not_4_out);
  and and_14 (and_14_out, and_8_out, B2);
  and and_15 (and_15_out, B2, and_9_out);
  or or_1 (or_1_out, and_10_out, and_11_out);
  or or_2 (R2, and_12_out, and_13_out);
  or or_3 (or_3_out, and_14_out, and_15_out);
  and and_16 (R4, A2, B2);
  or or_4 (R3, or_3_out, or_1_out);

  // Notes on the sheet:
  //   Karnaugh R1
  //   Karnaugh R2
  //   Karnaugh R3
  //   Karnaugh R4
  //   Karnaugh R1
  //   Karnaugh R2
  //   Karnaugh R3
  //   Karnaugh R4
endmodule
