// Logisim project Complemento de 2 Completo.circ as structural Verilog: 1 circuit, main circuit main
module main (
  input  A_1,
  input  A_2,
  input  A_3,
  input  A_4,
  output B_1,
  output B_2,
  output B_3,
  output B_4
);

  wire and_1_out, and_2_out, and_3_out, and_4_out, and_5_out, and_6_out, and_7_out, and_8_out, and_9_out,
       not_1_out, not_2_out, not_3_out, not_4_out, not_5_out, not_6_out, not_7_out, not_8_out, not_9_out;

  not not_1 (not_1_out, A_1);
  not not_2 (not_2_out, A_4);
  not not_3 (not_3_out, A_2);
  not not_4 (not_4_out, A_4);
  not not_5 (not_5_out, A_3);
  not not_6 (not_6_out, A_4);
  not not_7 (not_7_out, A_2);
  not not_8 (not_8_out, A_3);
  not not_9 (not_9_out, A_3);
  and and_1 (and_1_out, not_1_out, A_3);
  and and_2 (and_2_out, not_1_out, A_2);
  and and_3 (and_3_out, not_1_out, A_4);
  and and_4 (and_4_out, not_7_out, not_8_out, not_2_out, A_1);
  and and_5 (and_5_out, not_3_out, A_3);
  and and_6 (and_6_out, not_3_out, A_4);
  and and_7 (and_7_out, A_2, not_9_out, not_4_out);
  and and_8 (and_8_out, not_5_out, A_4);
  and and_9 (and_9_out, A_3, not_6_out);
  or or_1 (B_3, and_8_out, and_9_out);
  or or_2 (B_1, and_1_out, and_2_out, and_3_out, and_4_out);
  or or_3 (B_2, and_5_out, and_6_out, and_7_out);

  assign B_4 = A_4;

  // Notes on the sheet:
  //   Bit Número 01
  //   Bit Número 02
  //   Bit Número 03
  //   Bit Número 04
  //   Saída 01
  //   Saída 02
  //   Saída 03
  //   Saída 04
endmodule
