// Logisim project Complemento de 2.circ as structural Verilog: 1 circuit, main circuit main
module main (
  input  Bit_02,
  input  Bit_01,
  output Saida_02,
  output Saida_01
);

  wire not_1_out, not_2_out;

  not not_1 (not_1_out, Saida_01);
  xor xor_1 (Saida_01, 1'b1, Bit_01);
  not not_2 (not_2_out, Saida_02);
  xor xor_2 (Saida_02, not_1_out, Bit_02);
endmodule
