// Logisim project Somador Completo.circ as structural Verilog: 1 circuit, main circuit main
module main (
  input  A,
  input  B,
  input  Cin,
  output Cout,
  output S
);

  wire and_1_out, and_2_out, and_3_out, and_4_out, and_5_out, not_1_out, not_2_out, xor_1_out;

  not not_1 (not_1_out, A);
  and and_1 (and_1_out, A, B);
  and and_2 (and_2_out, A, Cin);
  and and_3 (and_3_out, Cin, B);
  not not_2 (not_2_out, xor_1_out);
  xor xor_1 (xor_1_out, B, Cin);
  or or_1 (Cout, and_1_out, and_2_out, and_3_out);
  and and_4 (and_4_out, A, not_2_out);
  and and_5 (and_5_out, xor_1_out, not_1_out);
  or or_2 (S, and_4_out, and_5_out);

  // Notes on the sheet:
  //   Somador Completo
endmodule
