// Logisim project somador de 4 bits.circ as structural Verilog: 1 circuit, main circuit main
module main (
  input  A3,
  input  A2,
  input  A1,
  input  A0,
  input  B3,
  input  B2,
  input  B1,
  input  B0,
  output S4,
  output S3,
  output S2,
  output S1,
  output S0
);

  wire and_1_out, and_2_out, and_3_out, and_4_out, and_5_out, and_6_out, and_7_out, and_8_out, and_9_out,
       and_10_out, and_11_out, and_12_out, and_13_out, not_1_out, not_2_out, not_3_out, not_4_out, not_5_out,
       not_6_out, or_3_out, or_4_out, or_6_out, or_7_out, or_9_out, xor_1_out, xor_2_out, xor_3_out;

  or or_1 (S4, and_1_out, and_2_out);
  or or_2 (S3, and_3_out, and_4_out);
  and and_1 (and_1_out, A3, or_3_out);
  and and_2 (and_2_out, or_4_out, B3);
  and and_3 (and_3_out, xor_1_out, not_2_out);
  and and_4 (and_4_out, not_1_out, A3);
  or or_3 (or_3_out, B3, or_4_out);
  not not_1 (not_1_out, xor_1_out);
  xor xor_1 (xor_1_out, B3, or_4_out);
  not not_2 (not_2_out, A3);
  or or_4 (or_4_out, and_5_out, and_6_out);
  or or_5 (S2, and_7_out, and_8_out);
  and and_5 (and_5_out, A2, or_6_out);
  and and_6 (and_6_out, or_7_out, B2);
  and and_7 (and_7_out, xor_2_out, not_4_out);
  not not_3 (not_3_out, xor_2_out);
  and and_8 (and_8_out, not_3_out, A2);
  or or_6 (or_6_out, B2, or_7_out);
  xor xor_2 (xor_2_out, B2, or_7_out);
  not not_4 (not_4_out, A2);
  or or_7 (or_7_out, and_9_out, and_10_out);
  or or_8 (S1, and_11_out, and_12_out);
  and and_9 (and_9_out, A1, or_9_out);
  and and_10 (and_10_out, and_13_out, B1);
  and and_11 (and_11_out, xor_3_out, not_6_out);
  and and_12 (and_12_out, not_5_out, A1);
  or or_9 (or_9_out, B1, and_13_out);
  not not_5 (not_5_out, xor_3_out);
  xor xor_3 (xor_3_out, B1, and_13_out);
  not not_6 (not_6_out, A1);
  and and_13 (and_13_out, A0, B0);
  xor xor_4 (S0, A0, B0);
endmodule
